# Fritzing sketch scrap (saved by Fritzing 0.9.3b)
circuit board: 7cm x 5cm
breadboards: 1

parts:
  Nano = Arduino Nano (Rev3.0)
  U1 = L9110 H-bridge module [part_number="L9110 H-bridge"]
  Battery = male pin header, 2 pins [form="♂ (male)"]
  Switch = male pin header, 2 pins [form="♂ (male)"]
  Servo_Header = male pin header, 3 pins [form="♂ (male)"]
  Sensor_Header = male pin header, 3 pins [form="♂ (male)"]

nets:
  GND: Nano.GND, U1.GND, Switch.pin2, Servo_Header.pin1, Sensor_Header.pin1
  IA-B: Nano.D2, U1.A-IB
  IA-A: Nano.D3, U1.A-IA
  IB-B: Nano.D6, U1.B-IB
  IB-A: Nano.D7, U1.B-IA
  HC-SR04: Nano.D11/MOSI, Sensor_Header.pin3
  Servo: Nano.D12/MISO, Servo_Header.pin3
  7.4V: Nano.VIN, U1.VCC, Battery.pin1
  5V: Nano.5V, Servo_Header.pin2, Sensor_Header.pin2
  N1: Battery.pin2, Switch.pin1
